// Logisim project Processor.circ as structural Verilog: 3 circuits, main circuit Processor
module Processor (
);

  wire clock_1_out;
  wire [1:0] func_q_2;
  wire [3:0] func_q, multiplexer_2_out, sll1_1_out_2;
  wire [5:0] Op_q;
  wire [15:0] Imm_q;
  wire [31:0] A_q, B_q, bit_extender_1_out, IF_ID_q, mipsprogramrom_1_p2, multiplexer_1_out, pc_4_1_new,
       PC_q, registerfile_1_p3, registerfile_1_p4;

  Register #(.width(32)) PC (.D(pc_4_1_new), .Q(PC_q), .clk(clock_1_out));  // open: en, clr
  Clock clock_1 (.out(clock_1_out));
  PC_4 pc_4_1 (.Old(PC_q), .New(pc_4_1_new));
  // MIPSProgramROM mipsprogramrom_1: pin names not known; wires that end beside it: PC_q, mipsprogramrom_1_p2
  Register #(.width(32)) IF_ID (.D(mipsprogramrom_1_p2), .Q(IF_ID_q));  // open: en, clk, clr
  // RegisterFile registerfile_1: pin names not known; wires that end beside it: IF_ID_q[20:16], IF_ID_q[15:11], registerfile_1_p3, registerfile_1_p4
  Register #(.width(32)) A (.D(registerfile_1_p3), .Q(A_q));  // open: en, clk, clr
  Register #(.width(32)) B (.D(registerfile_1_p4), .Q(B_q));  // open: en, clk, clr
  Register #(.width(16)) Imm (.D({IF_ID_q[10:0], IF_ID_q[15:11]}), .Q(Imm_q));  // open: en, clk, clr
  Register #(.width(5)) Rb (.D(IF_ID_q[25:21]));  // open: en, Q, clk, clr
  Register #(.width(6)) Op (.D(IF_ID_q[31:26]), .Q(Op_q));  // open: en, clk, clr
  Register #(.width(5)) shamt (.D(IF_ID_q[10:6]));  // open: en, Q, clk, clr
  Register #(.width(6)) func (.D(IF_ID_q[5:0]), .Q({func_q_2, func_q}));  // open: en, clk, clr
  assign bit_extender_1_out = {{16{Imm_q[15]}}, Imm_q};  // Bit_Extender bit_extender_1
  Multiplexer #(.width(32), .enable("false")) multiplexer_1 (
    .in0(B_q), .in1(bit_extender_1_out), .out(multiplexer_1_out), .sel(Op_q[3]));
  SLL1 sll1_1 (.in_1(func_q), .out_2(sll1_1_out_2));
  Multiplexer #(.width(4), .enable("false")) multiplexer_2 (
    .in0(sll1_1_out_2), .out(multiplexer_2_out));  // open: in1, sel
  // Mips_ALU mips_alu_1: pin names not known; wires that end beside it: A_q, multiplexer_1_out, multiplexer_2_out
  // LCD_Video lcd_video_1: pin names not known
endmodule

module PC_4 (
  input  [31:0] Old,
  output [31:0] New
);

  // Incrementer incrementer_1: pin names not known; wires that end beside it: Old[31:2], New[31:2]

  assign New[1:0] = Old[1:0];
endmodule

module SLL1 (
  input  [3:0] in_1,
  output [3:0] out_2
);

  wire not_1_out;

  not not_1 (not_1_out, in_1[3]);
  and and_1 (out_2[0], in_1[3], not_1_out);

  assign out_2[3:1] = in_1[2:0];
endmodule
